// Logisim project CPU .circ as structural Verilog: 38 circuits, main circuit main
module main (
  input  [7:0] in_1,
  input  [7:0] in_2,
  input  in_3,
  input  in_4,
  input  in_5,
  input  in_6,
  output [7:0] out_7
);

  // OR_Gate or_1 has open pins: in1=in_6, out=open
  RAM #(.bus("separate")) ram_1 (
    .addr(in_1), .din(in_2), .data(out_7), .str(in_3), .sel(1'b1), .clk(in_3), .ld(in_6), .clr(in_4));
endmodule

module MEM_1_BIT (
  input  D,
  input  E,
  output out_3
);

  wire nand_1_out, nand_2_out, nand_4_out;

  nand nand_1 (nand_1_out, D, E);
  nand nand_2 (nand_2_out, nand_1_out, E);
  nand nand_3 (out_3, nand_1_out, nand_4_out);
  nand nand_4 (nand_4_out, out_3, nand_2_out);
endmodule

module MEM_1_BYTE (
  input  [7:0] in_1,
  input  in_2,
  output [7:0] out_3
);

  MEM_1_BIT mem_1_bit_1 (.D(in_1[0]), .E(in_2), .out_3(out_3[0]));
  MEM_1_BIT mem_1_bit_2 (.D(in_1[1]), .E(in_2), .out_3(out_3[1]));
  MEM_1_BIT mem_1_bit_3 (.D(in_1[2]), .E(in_2), .out_3(out_3[2]));
  MEM_1_BIT mem_1_bit_4 (.D(in_1[3]), .E(in_2), .out_3(out_3[3]));
  MEM_1_BIT mem_1_bit_5 (.D(in_1[4]), .E(in_2), .out_3(out_3[4]));
  MEM_1_BIT mem_1_bit_6 (.D(in_1[5]), .E(in_2), .out_3(out_3[5]));
  MEM_1_BIT mem_1_bit_7 (.D(in_1[6]), .E(in_2), .out_3(out_3[6]));
  MEM_1_BIT mem_1_bit_8 (.D(in_1[7]), .E(in_2), .out_3(out_3[7]));
endmodule

module ENABLE (
  input  [7:0] in_1,
  input  in_2,
  output [7:0] out_3
);

  wire and_1_out, and_2_out, and_3_out, and_4_out, and_5_out, and_6_out, and_7_out, and_8_out;

  and and_1 (and_1_out, in_1[0], in_2);
  and and_2 (and_2_out, in_1[1], in_2);
  and and_3 (and_3_out, in_1[2], in_2);
  and and_4 (and_4_out, in_1[3], in_2);
  and and_5 (and_5_out, in_1[4], in_2);
  and and_6 (and_6_out, in_1[5], in_2);
  and and_7 (and_7_out, in_1[6], in_2);
  and and_8 (and_8_out, in_1[7], in_2);
  assign out_3[0] = in_2 ? and_1_out : 1'bz;  // Controlled_Buffer controlled_buffer_1
  assign out_3[1] = in_2 ? and_2_out : 1'bz;  // Controlled_Buffer controlled_buffer_2
  assign out_3[2] = in_2 ? and_3_out : 1'bz;  // Controlled_Buffer controlled_buffer_3
  assign out_3[3] = in_2 ? and_4_out : 1'bz;  // Controlled_Buffer controlled_buffer_4
  assign out_3[4] = in_2 ? and_5_out : 1'bz;  // Controlled_Buffer controlled_buffer_5
  assign out_3[5] = in_2 ? and_6_out : 1'bz;  // Controlled_Buffer controlled_buffer_6
  assign out_3[6] = in_2 ? and_7_out : 1'bz;  // Controlled_Buffer controlled_buffer_7
  assign out_3[7] = in_2 ? and_8_out : 1'bz;  // Controlled_Buffer controlled_buffer_8
endmodule

module REGISTER_8 (
  input  [7:0] in_1,
  input  in_2,
  input  in_3,
  output [7:0] out_4,
  output [7:0] out_5
);

  wire [7:0] enable_1_out_3;

  MEM_1_BYTE mem_1_byte_1 (.in_1(in_1), .out_3(out_4), .in_2(in_2));
  ENABLE enable_1 (.in_1(out_4), .out_3(enable_1_out_3), .in_2(in_3));
  assign out_5 = in_3 ? enable_1_out_3 : 8'bz;  // Controlled_Buffer controlled_buffer_1
endmodule

module DECODER_4x16 (
  input  [3:0] in_1,
  output L,
  output out_3,
  output out_4,
  output out_5,
  output out_6,
  output out_7,
  output out_8,
  output out_9,
  output out_10,
  output out_11,
  output out_12,
  output out_13,
  output out_14,
  output out_15,
  output out_16,
  output M
);

  wire not_1_out, not_2_out, not_3_out, not_4_out;

  not not_1 (not_1_out, in_1[0]);
  not not_2 (not_2_out, in_1[1]);
  not not_3 (not_3_out, in_1[2]);
  not not_4 (not_4_out, in_1[3]);
  and and_1 (L, not_4_out, not_3_out, not_2_out, not_1_out);
  and and_2 (out_3, not_4_out, not_3_out, not_2_out, in_1[0]);
  and and_3 (out_4, not_4_out, not_3_out, in_1[1], not_1_out);
  and and_4 (out_5, not_4_out, not_3_out, in_1[1], in_1[0]);
  and and_5 (out_6, not_4_out, in_1[2], not_2_out, not_1_out);
  and and_6 (out_7, not_4_out, in_1[2], not_2_out, in_1[0]);
  and and_7 (out_8, not_4_out, in_1[2], in_1[1], not_1_out);
  and and_8 (out_9, not_4_out, in_1[2], in_1[1], in_1[0]);
  and and_9 (out_10, in_1[3], not_3_out, not_2_out, not_1_out);
  and and_10 (out_11, in_1[3], not_3_out, not_2_out, in_1[0]);
  and and_11 (out_12, in_1[3], not_3_out, in_1[1], not_1_out);
  and and_12 (out_13, in_1[3], not_3_out, in_1[1], in_1[0]);
  and and_13 (out_14, in_1[3], in_1[2], not_2_out, not_1_out);
  and and_14 (out_15, in_1[3], in_1[2], not_2_out, in_1[0]);
  and and_15 (out_16, in_1[3], in_1[2], in_1[1], not_1_out);
  and and_16 (M, in_1[3], in_1[2], in_1[1], in_1[0]);

  // Notes on the sheet:
  //   out_6: pull=down
  //   M: pull=down
  //   out_9: pull=down
  //   out_13: pull=down
  //   out_14: pull=down
  //   L: pull=down
  //   out_5: pull=down
  //   out_4: pull=down
  //   out_16: pull=down
  //   out_11: pull=down
  //   out_7: pull=down
  //   out_15: pull=down
  //   out_3: pull=down
  //   out_8: pull=down
  //   out_10: pull=down
  //   out_12: pull=down
  //   in_1: pull=down
endmodule

module HALF_ADDER (
  input  in_1,
  input  in_2,
  output out_3,
  output out_4
);

  xor xor_1 (out_3, in_1, in_2);
  and and_1 (out_4, in_1, in_2);
endmodule

module FULL_ADDER (
  input  in_1,
  input  in_2,
  input  in_3,
  output out_4,
  output out_5
);

  wire half_adder_1_out_3, half_adder_1_out_4, half_adder_2_out_4;

  HALF_ADDER half_adder_1 (.in_1(in_1), .in_2(in_2), .out_3(half_adder_1_out_3), .out_4(half_adder_1_out_4));
  HALF_ADDER half_adder_2 (.in_1(half_adder_1_out_3), .in_2(in_3), .out_3(out_4), .out_4(half_adder_2_out_4));
  or or_1 (out_5, half_adder_2_out_4, half_adder_1_out_4);
endmodule

module RIPPLE_ADDER_8 (
  input  [7:0] in_1,
  input  in_2,
  input  [7:0] in_3,
  output [7:0] out_4,
  output out_5
);

  wire full_adder_1_out_5, full_adder_2_out_5, full_adder_3_out_5, full_adder_4_out_5, full_adder_5_out_5,
       full_adder_6_out_5, full_adder_7_out_5;

  FULL_ADDER full_adder_1 (.in_1(in_3[0]), .in_2(in_1[0]), .in_3(in_2), .out_4(out_4[0]), .out_5(full_adder_1_out_5));
  FULL_ADDER full_adder_2 (
    .in_1(in_3[1]), .in_2(in_1[1]), .in_3(full_adder_1_out_5), .out_4(out_4[1]), .out_5(full_adder_2_out_5));
  FULL_ADDER full_adder_3 (
    .in_1(in_3[2]), .in_2(in_1[2]), .in_3(full_adder_2_out_5), .out_4(out_4[2]), .out_5(full_adder_3_out_5));
  FULL_ADDER full_adder_4 (
    .in_1(in_3[3]), .in_2(in_1[3]), .in_3(full_adder_3_out_5), .out_4(out_4[3]), .out_5(full_adder_4_out_5));
  FULL_ADDER full_adder_5 (
    .in_1(in_3[4]), .in_2(in_1[4]), .in_3(full_adder_4_out_5), .out_4(out_4[4]), .out_5(full_adder_5_out_5));
  FULL_ADDER full_adder_6 (
    .in_1(in_3[5]), .in_2(in_1[5]), .in_3(full_adder_5_out_5), .out_4(out_4[5]), .out_5(full_adder_6_out_5));
  FULL_ADDER full_adder_7 (
    .in_1(in_3[6]), .in_2(in_1[6]), .in_3(full_adder_6_out_5), .out_4(out_4[6]), .out_5(full_adder_7_out_5));
  FULL_ADDER full_adder_8 (.in_1(in_3[7]), .in_2(in_1[7]), .in_3(full_adder_7_out_5), .out_4(out_4[7]), .out_5(out_5));
endmodule

module ALU_ADD_SUB_RIPPLE (
  input  Cin,
  input  [7:0] in_2,
  input  SUB_SIGN,
  input  [7:0] in_4,
  output [7:0] out_5,
  output out_6
);

  wire and_1_out, not_1_out, or_1_out;
  wire [7:0] xor_8_out;

  xor xor_1 (xor_8_out[7], SUB_SIGN, in_4[7]);
  xor xor_2 (xor_8_out[6], SUB_SIGN, in_4[6]);
  xor xor_3 (xor_8_out[5], SUB_SIGN, in_4[5]);
  not not_1 (not_1_out, SUB_SIGN);
  and and_1 (and_1_out, not_1_out, Cin);
  or or_1 (or_1_out, SUB_SIGN, and_1_out);
  xor xor_4 (xor_8_out[4], SUB_SIGN, in_4[4]);
  RIPPLE_ADDER_8 ripple_adder_8_1 (.in_1(xor_8_out), .in_2(or_1_out), .in_3(in_2), .out_4(out_5), .out_5(out_6));
  xor xor_5 (xor_8_out[3], SUB_SIGN, in_4[3]);
  xor xor_6 (xor_8_out[2], SUB_SIGN, in_4[2]);
  xor xor_7 (xor_8_out[1], SUB_SIGN, in_4[1]);
  xor xor_8 (xor_8_out[0], SUB_SIGN, in_4[0]);

  // Notes on the sheet:
  //   Cin: pull=down
endmodule

module ALU_SH_R (
  input  [7:0] in_1,
  input  in_2,
  output out_3,
  output [7:0] out_4
);

  wire [7:1] register_8_1_out_5;

  REGISTER_8 register_8_1 (.in_1(in_1), .in_2(1'b1), .in_3(1'b1), .out_5({register_8_1_out_5, out_3}));  // open: out_4
  REGISTER_8 register_8_2 (.in_1({in_2, register_8_1_out_5}), .in_2(1'b1), .in_3(1'b1), .out_5(out_4));  // open: out_4
endmodule

module ALU_SH_L (
  input  in_1,
  input  [7:0] in_2,
  output [7:0] out_3,
  output out_4
);

  wire [6:0] register_8_1_out_5;

  REGISTER_8 register_8_1 (.in_1(in_2), .in_2(1'b1), .in_3(1'b1), .out_5({out_4, register_8_1_out_5}));  // open: out_4
  REGISTER_8 register_8_2 (.in_1({register_8_1_out_5, in_1}), .in_2(1'b1), .in_3(1'b1), .out_5(out_3));  // open: out_4
endmodule

module ALU_XOR_COMP_1 (
  input  Prev_equal,
  input  Prev_greater,
  input  A,
  input  B,
  output Comp_res,
  output out_6,
  output Equals
);

  wire and_2_out, not_1_out;

  xor xor_1 (Comp_res, A, B);
  not not_1 (not_1_out, Comp_res);
  and and_1 (Equals, not_1_out, Prev_equal);
  and and_2 (and_2_out, A, Comp_res, Prev_equal);
  or or_1 (out_6, and_2_out, Prev_greater);
endmodule

module ALU_XOR_COMP_8 (
  input  [7:0] in_1,
  input  [7:0] in_2,
  output [7:0] out_3,
  output out_4,
  output out_5
);

  wire alu_xor_comp_1_1_equals, alu_xor_comp_1_1_out_6, alu_xor_comp_1_2_equals, alu_xor_comp_1_2_out_6,
       alu_xor_comp_1_3_equals, alu_xor_comp_1_3_out_6, alu_xor_comp_1_4_equals, alu_xor_comp_1_4_out_6,
       alu_xor_comp_1_5_equals, alu_xor_comp_1_5_out_6, alu_xor_comp_1_6_equals, alu_xor_comp_1_6_out_6,
       alu_xor_comp_1_7_equals, alu_xor_comp_1_7_out_6;

  ALU_XOR_COMP_1 alu_xor_comp_1_1 (
    .A(in_2[7]), .B(in_1[7]), .Comp_res(out_3[7]), .out_6(alu_xor_comp_1_1_out_6),
    .Equals(alu_xor_comp_1_1_equals), .Prev_equal(1'b1), .Prev_greater(1'b0));
  ALU_XOR_COMP_1 alu_xor_comp_1_2 (
    .A(in_2[6]), .B(in_1[6]), .Comp_res(out_3[6]), .out_6(alu_xor_comp_1_2_out_6),
    .Equals(alu_xor_comp_1_2_equals), .Prev_equal(alu_xor_comp_1_1_equals),
    .Prev_greater(alu_xor_comp_1_1_out_6));
  ALU_XOR_COMP_1 alu_xor_comp_1_3 (
    .A(in_2[5]), .B(in_1[5]), .Comp_res(out_3[5]), .out_6(alu_xor_comp_1_3_out_6),
    .Equals(alu_xor_comp_1_3_equals), .Prev_equal(alu_xor_comp_1_2_equals),
    .Prev_greater(alu_xor_comp_1_2_out_6));
  ALU_XOR_COMP_1 alu_xor_comp_1_4 (
    .A(in_2[4]), .B(in_1[4]), .Comp_res(out_3[4]), .out_6(alu_xor_comp_1_4_out_6),
    .Equals(alu_xor_comp_1_4_equals), .Prev_equal(alu_xor_comp_1_3_equals),
    .Prev_greater(alu_xor_comp_1_3_out_6));
  ALU_XOR_COMP_1 alu_xor_comp_1_5 (
    .A(in_2[3]), .B(in_1[3]), .Comp_res(out_3[3]), .out_6(alu_xor_comp_1_5_out_6),
    .Equals(alu_xor_comp_1_5_equals), .Prev_equal(alu_xor_comp_1_4_equals),
    .Prev_greater(alu_xor_comp_1_4_out_6));
  ALU_XOR_COMP_1 alu_xor_comp_1_6 (
    .A(in_2[2]), .B(in_1[2]), .Comp_res(out_3[2]), .out_6(alu_xor_comp_1_6_out_6),
    .Equals(alu_xor_comp_1_6_equals), .Prev_equal(alu_xor_comp_1_5_equals),
    .Prev_greater(alu_xor_comp_1_5_out_6));
  ALU_XOR_COMP_1 alu_xor_comp_1_7 (
    .A(in_2[1]), .B(in_1[1]), .Comp_res(out_3[1]), .out_6(alu_xor_comp_1_7_out_6),
    .Equals(alu_xor_comp_1_7_equals), .Prev_equal(alu_xor_comp_1_6_equals),
    .Prev_greater(alu_xor_comp_1_6_out_6));
  ALU_XOR_COMP_1 alu_xor_comp_1_8 (
    .A(in_2[0]), .B(in_1[0]), .Comp_res(out_3[0]), .out_6(out_4), .Equals(out_5),
    .Prev_equal(alu_xor_comp_1_7_equals), .Prev_greater(alu_xor_comp_1_7_out_6));
endmodule

module ALU_ZERO_FLAG (
  input  [7:0] in_1,
  output out_2
);

  nor nor_1 (out_2, in_1[0], in_1[1], in_1[2], in_1[3], in_1[4], in_1[5], in_1[6], in_1[7]);
endmodule

module ALU_AND (
  input  [7:0] in_1,
  input  [7:0] in_2,
  output [7:0] out_3
);

  and and_1 (out_3[0], in_1[0], in_2[0]);
  and and_2 (out_3[1], in_1[1], in_2[1]);
  and and_3 (out_3[2], in_1[2], in_2[2]);
  and and_4 (out_3[3], in_1[3], in_2[3]);
  and and_5 (out_3[4], in_1[4], in_2[4]);
  and and_6 (out_3[5], in_1[5], in_2[5]);
  and and_7 (out_3[6], in_1[6], in_2[6]);
  and and_8 (out_3[7], in_1[7], in_2[7]);
endmodule

module ALU_OR (
  input  [7:0] in_1,
  input  [7:0] in_2,
  output [7:0] out_3
);

  or or_1 (out_3[0], in_1[0], in_2[0]);
  or or_2 (out_3[1], in_1[1], in_2[1]);
  or or_3 (out_3[2], in_1[2], in_2[2]);
  or or_4 (out_3[3], in_1[3], in_2[3]);
  or or_5 (out_3[4], in_1[4], in_2[4]);
  or or_6 (out_3[5], in_1[5], in_2[5]);
  or or_7 (out_3[6], in_1[6], in_2[6]);
  or or_8 (out_3[7], in_1[7], in_2[7]);
endmodule

module ALU (
  input  [7:0] in_1,
  input  [7:0] in_2,
  input  in_3,
  input  [2:0] Instruction,
  output A_greater,
  output equals,
  output zero,
  output [7:0] \output ,
  output Cout
);

  wire alu_add_sub_ripple_1_out_6, alu_sh_l_1_out_4, alu_sh_r_1_out_3, and_1_out, and_2_out, and_3_out,
       decoder_1_out0, decoder_1_out1, decoder_1_out2, decoder_1_out3, decoder_1_out4, decoder_1_out5,
       decoder_1_out6, decoder_1_out7, or_1_out;
  wire [7:0] alu_add_sub_ripple_1_out_5, alu_and_1_out_3, alu_not_1_out_2, alu_or_1_out_3, alu_sh_l_1_out_3,
       alu_sh_r_1_out_4, alu_xor_comp_8_1_out_3;

  ALU_AND alu_and_1 (.in_1(in_1), .in_2(in_2), .out_3(alu_and_1_out_3));
  ALU_OR alu_or_1 (.in_1(in_1), .in_2(in_2), .out_3(alu_or_1_out_3));
  ALU_XOR_COMP_8 alu_xor_comp_8_1 (
    .in_1(in_2), .in_2(in_1), .out_3(alu_xor_comp_8_1_out_3), .out_5(equals), .out_4(A_greater));
  ALU_NOT alu_not_1 (.in_1(in_1), .out_2(alu_not_1_out_2));
  ALU_SH_L alu_sh_l_1 (.in_1(in_3), .in_2(in_1), .out_3(alu_sh_l_1_out_3), .out_4(alu_sh_l_1_out_4));
  ALU_SH_R alu_sh_r_1 (.in_1(in_1), .out_3(alu_sh_r_1_out_3), .out_4(alu_sh_r_1_out_4), .in_2(in_3));
  ALU_ADD_SUB_RIPPLE alu_add_sub_ripple_1 (
    .in_2(in_1), .SUB_SIGN(decoder_1_out1), .out_5(alu_add_sub_ripple_1_out_5),
    .out_6(alu_add_sub_ripple_1_out_6), .in_4(in_2), .Cin(in_3));
  Decoder #(.select(3), .disabled(0)) decoder_1 (
    .out0(decoder_1_out0), .out1(decoder_1_out1), .out2(decoder_1_out2), .out3(decoder_1_out3),
    .out4(decoder_1_out4), .out5(decoder_1_out5), .out6(decoder_1_out6), .out7(decoder_1_out7),
    .sel(Instruction), .en(1'b1));
  or or_1 (or_1_out, decoder_1_out0, decoder_1_out1);
  ENABLE enable_1 (.in_1(alu_xor_comp_8_1_out_3), .out_3(\output ), .in_2(decoder_1_out7));
  ENABLE enable_2 (.in_1(alu_and_1_out_3), .out_3(\output ), .in_2(decoder_1_out6));
  ENABLE enable_3 (.in_1(alu_or_1_out_3), .out_3(\output ), .in_2(decoder_1_out5));
  ENABLE enable_4 (.in_1(alu_not_1_out_2), .out_3(\output ), .in_2(decoder_1_out4));
  ENABLE enable_5 (.in_1(alu_sh_l_1_out_3), .out_3(\output ), .in_2(decoder_1_out3));
  ENABLE enable_6 (.in_1(alu_sh_r_1_out_4), .out_3(\output ), .in_2(decoder_1_out2));
  ENABLE enable_7 (.in_1(alu_add_sub_ripple_1_out_5), .out_3(\output ), .in_2(or_1_out));
  and and_1 (and_1_out, decoder_1_out3, alu_sh_l_1_out_4);
  assign Cout = decoder_1_out3 ? and_1_out : 1'bz;  // Controlled_Buffer controlled_buffer_1
  assign Cout = decoder_1_out2 ? and_2_out : 1'bz;  // Controlled_Buffer controlled_buffer_2
  and and_2 (and_2_out, decoder_1_out2, alu_sh_r_1_out_3);
  assign Cout = or_1_out ? and_3_out : 1'bz;  // Controlled_Buffer controlled_buffer_3
  and and_3 (and_3_out, or_1_out, alu_add_sub_ripple_1_out_6);
  ALU_ZERO_FLAG alu_zero_flag_1 (.in_1(\output ), .out_2(zero));

  // Notes on the sheet:
  //   in_1: pull=down
  //   Instruction: pull=down
  //   in_3: pull=down
  //   in_2: pull=down
endmodule

module ALU_NOT (
  input  [7:0] in_1,
  output [7:0] out_2
);

  not not_1 (out_2[0], in_1[0]);
  not not_2 (out_2[1], in_1[1]);
  not not_3 (out_2[2], in_1[2]);
  not not_4 (out_2[3], in_1[3]);
  not not_5 (out_2[4], in_1[4]);
  not not_6 (out_2[5], in_1[5]);
  not not_7 (out_2[6], in_1[6]);
  not not_8 (out_2[7], in_1[7]);
endmodule

module CLK (
  input  CLKin,
  output CLK,
  output CLKs,
  output CLKe
);

  wire j_k_ff_1_qn;

  J_K_Flip_Flop j_k_ff_1 (.J(1'b1), .clk(CLKin), .K(1'b1), .Q(CLK), .Qn(j_k_ff_1_qn));  // open: preset, en, reset
  and and_1 (CLKs, CLKin, CLK);
  nand nand_1 (CLKe, j_k_ff_1_qn, CLKin);
endmodule

module RAM_MEM_BYTE_CELL (
  input  [7:0] in_1,
  input  RST,
  input  H,
  input  V,
  input  S,
  input  E,
  output [7:0] out_7
);

  wire and_1_out, and_2_out, and_3_out, or_1_out;
  wire [7:0] register_8_1_out_5;

  and and_1 (and_1_out, H, V);
  and and_2 (and_2_out, and_1_out, S);
  or or_1 (or_1_out, RST, and_2_out);
  and and_3 (and_3_out, and_1_out, E);
  REGISTER_8 register_8_1 (.in_1(in_1), .in_2(or_1_out), .in_3(and_3_out), .out_5(register_8_1_out_5));  // open: out_4
  assign out_7 = and_3_out ? register_8_1_out_5 : 8'bz;  // Controlled_Buffer controlled_buffer_1
endmodule

module RAM_64 (
  input  [7:0] address,
  input  [7:0] in_2,
  input  S,
  input  STA,
  input  E,
  input  RST,
  output [7:0] out_7
);

  wire [7:0] mem_1_byte_1_out_3;

  MEM_1_BYTE mem_1_byte_1 (.in_1(address), .out_3(mem_1_byte_1_out_3), .in_2(STA));
  RAM #(.bus("separate")) ram_1 (
    .addr(mem_1_byte_1_out_3), .din(in_2), .data(out_7), .str(S), .sel(1'b1), .clk(S), .ld(E), .clr(RST));
endmodule

module CPU_BUS_1 (
  input  [7:0] in_1,
  input  in_2,
  output [7:0] out_3
);

  wire not_1_out;

  and and_1 (out_3[7], in_1[7], not_1_out);
  and and_2 (out_3[6], in_1[6], not_1_out);
  and and_3 (out_3[5], in_1[5], not_1_out);
  and and_4 (out_3[4], in_1[4], not_1_out);
  and and_5 (out_3[3], in_1[3], not_1_out);
  and and_6 (out_3[1], in_1[1], not_1_out);
  and and_7 (out_3[2], in_1[2], not_1_out);
  or or_1 (out_3[0], in_1[0], in_2);
  not not_1 (not_1_out, in_2);
endmodule

module CPU_ACC (
  input  [7:0] in_1,
  input  in_2,
  input  in_3,
  output [7:0] out_4,
  output [7:0] out_5
);

  wire [7:0] controlled_buffer_1_out, register_8_1_out_5;

  assign controlled_buffer_1_out = in_2 ? in_1 : 8'bz;  // Controlled_Buffer controlled_buffer_1
  REGISTER_8 register_8_1 (
    .in_1(controlled_buffer_1_out), .in_2(in_2), .in_3(in_3), .out_5(register_8_1_out_5), .out_4(out_5));
  assign out_4 = in_3 ? register_8_1_out_5 : 8'bz;  // Controlled_Buffer controlled_buffer_2

  // Notes on the sheet:
  //   in_1: pull=down
endmodule

module CPU_TEMP (
  input  [7:0] in_1,
  input  in_2,
  output [7:0] out_3
);

  wire [7:0] controlled_buffer_1_out;

  assign controlled_buffer_1_out = in_2 ? in_1 : 8'bz;  // Controlled_Buffer controlled_buffer_1
  MEM_1_BYTE mem_1_byte_1 (.in_1(controlled_buffer_1_out), .out_3(out_3), .in_2(in_2));

  // Notes on the sheet:
  //   in_1: pull=down
endmodule

module COUNTER_8 (
  input  in_1,
  input  in_2,
  output out_3,
  output out_4,
  output out_5,
  output out_6,
  output out_7,
  output out_8,
  output out_9
);

  wire mem_1_bit_1_out_3, mem_1_bit_2_out_3, mem_1_bit_3_out_3, mem_1_bit_4_out_3, mem_1_bit_5_out_3,
       mem_1_bit_6_out_3, mem_1_bit_7_out_3, mem_1_bit_8_out_3, mem_1_bit_9_out_3, mem_1_bit_10_out_3,
       mem_1_bit_11_out_3, not_1_out, not_2_out, not_3_out, not_4_out, not_5_out, not_6_out, not_7_out,
       not_8_out, or_1_out, or_2_out;

  not not_1 (not_1_out, in_1);
  or or_1 (or_1_out, in_1, in_2);
  not not_2 (not_2_out, in_2);
  or or_2 (or_2_out, in_1, not_2_out);
  or or_3 (out_3, in_1, not_3_out);
  not not_3 (not_3_out, mem_1_bit_2_out_3);
  MEM_1_BIT mem_1_bit_1 (.D(not_1_out), .E(or_1_out), .out_3(mem_1_bit_1_out_3));
  MEM_1_BIT mem_1_bit_2 (.D(mem_1_bit_1_out_3), .E(or_2_out), .out_3(mem_1_bit_2_out_3));
  and and_1 (out_4, mem_1_bit_2_out_3, not_4_out);
  MEM_1_BIT mem_1_bit_3 (.D(mem_1_bit_2_out_3), .E(or_1_out), .out_3(mem_1_bit_3_out_3));
  not not_4 (not_4_out, mem_1_bit_4_out_3);
  MEM_1_BIT mem_1_bit_4 (.D(mem_1_bit_3_out_3), .E(or_2_out), .out_3(mem_1_bit_4_out_3));
  and and_2 (out_5, mem_1_bit_4_out_3, not_5_out);
  MEM_1_BIT mem_1_bit_5 (.D(mem_1_bit_4_out_3), .E(or_1_out), .out_3(mem_1_bit_5_out_3));
  not not_5 (not_5_out, mem_1_bit_6_out_3);
  MEM_1_BIT mem_1_bit_6 (.D(mem_1_bit_5_out_3), .E(or_2_out), .out_3(mem_1_bit_6_out_3));
  and and_3 (out_6, mem_1_bit_6_out_3, not_6_out);
  MEM_1_BIT mem_1_bit_7 (.D(mem_1_bit_6_out_3), .E(or_1_out), .out_3(mem_1_bit_7_out_3));
  not not_6 (not_6_out, mem_1_bit_8_out_3);
  MEM_1_BIT mem_1_bit_8 (.D(mem_1_bit_7_out_3), .E(or_2_out), .out_3(mem_1_bit_8_out_3));
  and and_4 (out_7, mem_1_bit_8_out_3, not_7_out);
  not not_7 (not_7_out, mem_1_bit_10_out_3);
  MEM_1_BIT mem_1_bit_9 (.D(mem_1_bit_8_out_3), .E(or_1_out), .out_3(mem_1_bit_9_out_3));
  MEM_1_BIT mem_1_bit_10 (.D(mem_1_bit_9_out_3), .E(or_2_out), .out_3(mem_1_bit_10_out_3));
  and and_5 (out_8, mem_1_bit_10_out_3, not_8_out);
  MEM_1_BIT mem_1_bit_11 (.D(mem_1_bit_10_out_3), .E(or_1_out), .out_3(mem_1_bit_11_out_3));
  not not_8 (not_8_out, out_9);
  MEM_1_BIT mem_1_bit_12 (.D(mem_1_bit_11_out_3), .E(or_2_out), .out_3(out_9));

  // Notes on the sheet:
  //   in_1: pull=up
endmodule

module CPU (
  input  in_1,
  output [7:0] out_2,
  output [7:0] out_3,
  output [7:0] out_4,
  output [7:0] out_5,
  output [7:0] out_6,
  output [7:0] out_7,
  output [7:0] out_8
);

  wire alu_1_a_greater, alu_1_cout, alu_1_equals, alu_1_zero, and_1_out, and_2_out, clk_1_clk, clk_1_clke,
       clk_1_clks, clock_1_out, cpu_carry_temp_1_out_3, cpu_flag_reg_1_out_6, cpu_flag_reg_1_out_7,
       cpu_flag_reg_1_out_8, cpu_flag_reg_1_out_9, cu_1_acce, cu_1_accs, cu_1_bus1, cu_1_flags, cu_1_iare,
       cu_1_iars, cu_1_irs, cu_1_mars, cu_1_out_21, cu_1_rame, cu_1_rams, cu_1_reg_e0, cu_1_reg_e1,
       cu_1_reg_e2, cu_1_reg_e3, cu_1_reg_s0, cu_1_reg_s3, cu_1_regs_1, cu_1_regs_2, cu_1_temps, END,
       not_1_out;
  wire [2:0] cu_1_out_31;
  wire [7:0] alu_1_output, cpu_acc_1_out_4, cpu_bus_1_1_out_3, cpu_temp_1_out_3;

  ALU alu_1 (
    .in_1(cpu_acc_1_out_4), .in_2(cpu_bus_1_1_out_3), .in_3(and_1_out), .Instruction(cu_1_out_31),
    .A_greater(alu_1_a_greater), .equals(alu_1_equals), .zero(alu_1_zero), .\output (alu_1_output),
    .Cout(alu_1_cout));
  CPU_TEMP cpu_temp_1 (.in_1(cpu_acc_1_out_4), .in_2(cu_1_temps), .out_3(cpu_temp_1_out_3));
  CPU_BUS_1 cpu_bus_1_1 (.in_1(cpu_temp_1_out_3), .in_2(cu_1_bus1), .out_3(cpu_bus_1_1_out_3));
  and and_1 (and_1_out, cpu_carry_temp_1_out_3, cu_1_out_21);
  CPU_ACC cpu_acc_1 (.in_1(alu_1_output), .in_2(cu_1_accs), .in_3(cu_1_acce), .out_4(cpu_acc_1_out_4), .out_5(out_6));
  CPU_CARRY_TEMP cpu_carry_temp_1 (.in_1(cpu_flag_reg_1_out_9), .in_2(cu_1_temps), .out_3(cpu_carry_temp_1_out_3));
  CPU_FLAG_REG cpu_flag_reg_1 (
    .in_1(alu_1_a_greater), .in_2(alu_1_equals), .in_3(alu_1_zero), .in_4(alu_1_cout), .in_5(cu_1_flags),
    .out_6(cpu_flag_reg_1_out_6), .out_7(cpu_flag_reg_1_out_7), .out_8(cpu_flag_reg_1_out_8),
    .out_9(cpu_flag_reg_1_out_9));
  Clock clock_1 (.out(clock_1_out));
  and and_2 (and_2_out, clock_1_out, not_1_out);
  not not_1 (not_1_out, END);
  CPU_REG cpu_reg_1 (
    .in_1(cpu_acc_1_out_4), .in_2(cu_1_reg_s0), .in_3(cu_1_reg_e0), .out_4(cpu_acc_1_out_4), .out_5(out_2));
  CLK clk_1 (.CLKin(and_2_out), .CLK(clk_1_clk), .CLKs(clk_1_clks), .CLKe(clk_1_clke));
  CU cu_1 (
    .CLK(clk_1_clk), .CLKe(clk_1_clke), .CLKs(clk_1_clks), .BUS1(cu_1_bus1), .IARe(cu_1_iare),
    .RAMe(cu_1_rame), .ACCe(cu_1_acce), .REG_e0(cu_1_reg_e0), .REG_e1(cu_1_reg_e1), .REG_e2(cu_1_reg_e2),
    .REG_e3(cu_1_reg_e3), .MARs(cu_1_mars), .TEMPs(cu_1_temps), .RAMs(cu_1_rams), .ACCs(cu_1_accs),
    .REG_s0(cu_1_reg_s0), .REGs_1(cu_1_regs_1), .REGs_2(cu_1_regs_2), .REG_s3(cu_1_reg_s3), .IARs(cu_1_iars),
    .IRs(cu_1_irs), .in_9(out_7), .out_31(cu_1_out_31), .gr(cpu_flag_reg_1_out_6), .eq(cpu_flag_reg_1_out_7),
    .zero(cpu_flag_reg_1_out_8), .C(cpu_flag_reg_1_out_9), .out_21(cu_1_out_21), .in_2(in_1),
    .FLAGs(cu_1_flags), .END(END));
  CPU_REG cpu_reg_2 (
    .in_1(cpu_acc_1_out_4), .in_2(cu_1_regs_1), .in_3(cu_1_reg_e1), .out_4(cpu_acc_1_out_4), .out_5(out_3));
  CPU_IAR cpu_iar_1 (
    .in_1(cpu_acc_1_out_4), .in_2(cu_1_iars), .in_3(cu_1_iare), .out_4(cpu_acc_1_out_4), .out_5(out_8));
  CPU_REG cpu_reg_3 (
    .in_1(cpu_acc_1_out_4), .in_2(cu_1_regs_2), .in_3(cu_1_reg_e2), .out_4(cpu_acc_1_out_4), .out_5(out_4));
  CPU_IR cpu_ir_1 (.in_1(cpu_acc_1_out_4), .in_2(cu_1_irs), .out_3(out_7));
  CPU_REG cpu_reg_4 (
    .in_1(cpu_acc_1_out_4), .in_2(cu_1_reg_s3), .in_3(cu_1_reg_e3), .out_4(cpu_acc_1_out_4), .out_5(out_5));
  RAM_64 ram_64_1 (
    .address(cpu_acc_1_out_4), .STA(cu_1_mars), .S(cu_1_rams), .E(cu_1_rame), .RST(in_1),
    .in_2(cpu_acc_1_out_4), .out_7(cpu_acc_1_out_4));

  // Other names for the same wires on the sheet: RESET = in_1
endmodule

module CPU_REG (
  input  [7:0] in_1,
  input  in_2,
  input  in_3,
  output [7:0] out_4,
  output [7:0] out_5
);

  wire [7:0] controlled_buffer_1_out, register_8_1_out_5;

  assign controlled_buffer_1_out = in_2 ? in_1 : 8'bz;  // Controlled_Buffer controlled_buffer_1
  REGISTER_8 register_8_1 (
    .in_1(controlled_buffer_1_out), .in_2(in_2), .in_3(in_3), .out_5(register_8_1_out_5), .out_4(out_5));
  assign out_4 = in_3 ? register_8_1_out_5 : 8'bz;  // Controlled_Buffer controlled_buffer_2

  // Notes on the sheet:
  //   in_2: pull=up
  //   in_1: pull=down
endmodule

module CPU_template (
  input  [2:0] in_1
);

  wire clk_1_clk, clk_1_clke, clk_1_clks, clock_1_out;
  wire [7:0] alu_1_output, cpu_acc_1_out_4, cpu_bus_1_1_out_3, cpu_temp_1_out_3;

  ALU alu_1 (
    .in_1({cpu_acc_1_out_4[7:2], cpu_acc_1_out_4[4], cpu_acc_1_out_4[0]}), .in_2(cpu_bus_1_1_out_3),
    .in_3(1'b0), .Instruction(in_1), .\output (alu_1_output));  // open: A_greater, equals, zero, Cout
  CPU_TEMP cpu_temp_1 (
    .in_1({cpu_acc_1_out_4[7:2], cpu_acc_1_out_4[4], cpu_acc_1_out_4[0]}), .out_3(cpu_temp_1_out_3));  // open: in_2
  CPU_BUS_1 cpu_bus_1_1 (.in_1(cpu_temp_1_out_3), .out_3(cpu_bus_1_1_out_3));  // open: in_2
  CPU_ACC cpu_acc_1 (
    .in_1(alu_1_output), .out_4({cpu_acc_1_out_4[7:2], cpu_acc_1_out_4[4], cpu_acc_1_out_4[0]}));  // open: in_2, in_3, out_5
  Clock clock_1 (.out(clock_1_out));
  CLK clk_1 (.CLKin(clock_1_out), .CLK(clk_1_clk), .CLKs(clk_1_clks), .CLKe(clk_1_clke));
  CPU_REG cpu_reg_1 (
    .in_1({cpu_acc_1_out_4[7:2], cpu_acc_1_out_4[4], cpu_acc_1_out_4[0]}),
    .out_4({cpu_acc_1_out_4[7:2], cpu_acc_1_out_4[4], cpu_acc_1_out_4[0]}));  // open: in_2, in_3, out_5
  CPU_REG cpu_reg_2 (
    .in_1({cpu_acc_1_out_4[7:2], cpu_acc_1_out_4[4], cpu_acc_1_out_4[0]}),
    .out_4({cpu_acc_1_out_4[7:2], cpu_acc_1_out_4[4], cpu_acc_1_out_4[0]}));  // open: in_2, in_3, out_5
  CPU_REG cpu_reg_3 (
    .in_1({cpu_acc_1_out_4[7:2], cpu_acc_1_out_4[4], cpu_acc_1_out_4[0]}),
    .out_4({cpu_acc_1_out_4[7:2], cpu_acc_1_out_4[4], cpu_acc_1_out_4[0]}));  // open: in_2, in_3, out_5
  CPU_REG cpu_reg_4 (
    .in_1({cpu_acc_1_out_4[7:2], cpu_acc_1_out_4[4], cpu_acc_1_out_4[0]}),
    .out_4({cpu_acc_1_out_4[7:2], cpu_acc_1_out_4[4], cpu_acc_1_out_4[0]}));  // open: in_2, in_3, out_5
  RAM_64 ram_64_1 ();  // open: address, STA, S, E, RST, in_2, out_7
endmodule

module CU_ADD (
  input  CLK,
  input  CLKe,
  input  CLKs,
  input  [7:0] in_4,
  output MARs,
  output BUS1,
  output TEMPs,
  output IARe,
  output RAMs,
  output RAMe,
  output ACCs,
  output ACCe,
  output REG_s0,
  output REG_e0,
  output REGs_1,
  output REG_e1,
  output REGs_2,
  output REG_e2,
  output REG_s3,
  output REG_e3,
  output IARs,
  output IRs
);

  wire counter_8_1_p3, counter_8_1_p4, counter_8_1_p5;

  and and_1 (IARe, CLKe, BUS1);
  and and_2 (RAMe, CLKe, counter_8_1_p3);
  and and_3 (ACCe, CLKe, counter_8_1_p4);
  and and_4 (REG_e0, CLKe, 1'b0);
  and and_5 (REG_e1, CLKe, 1'b0);
  and and_6 (REG_e2, CLKe, 1'b0);
  and and_7 (REG_e3, CLKe, 1'b0);
  // COUNTER_8 counter_8_1: pin names not known; wires that end beside it: CLK, BUS1, counter_8_1_p3, counter_8_1_p4, counter_8_1_p5
  and and_8 (MARs, CLKs, BUS1);
  buf and_9 (TEMPs, CLKs);  // AND_Gate
  and and_10 (RAMs, CLKs, 1'b0);
  and and_11 (ACCs, CLKs, BUS1);
  and and_12 (REG_s0, CLKs, 1'b0);
  and and_13 (REGs_1, CLKs, 1'b0);
  and and_14 (REGs_2, CLKs, 1'b0);
  and and_15 (REG_s3, CLKs, 1'b0);
  and and_16 (IARs, CLKs, counter_8_1_p4);
  and and_17 (IRs, CLKs, counter_8_1_p3);
endmodule

module CPU_IAR (
  input  [7:0] in_1,
  input  in_2,
  input  in_3,
  output [7:0] out_4,
  output [7:0] out_5
);

  REGISTER_8 register_8_1 (.in_1(in_1), .in_2(in_2), .in_3(in_3), .out_5(out_4), .out_4(out_5));

  // Notes on the sheet:
  //   in_1: pull=down
endmodule

module CPU_IR (
  input  [7:0] in_1,
  input  in_2,
  output [7:0] out_3
);

  MEM_1_BYTE mem_1_byte_1 (.in_1(in_1), .out_3(out_3), .in_2(in_2));

  // Notes on the sheet:
  //   in_1: pull=down
endmodule

module CPU_MAR (
  input  [7:0] in_1,
  input  in_2,
  output [7:0] out_3
);

  MEM_1_BYTE mem_1_byte_1 (.in_1(in_1), .out_3(out_3), .in_2(in_2));

  // Notes on the sheet:
  //   in_1: pull=down
endmodule

module CU (
  input  CLK,
  input  in_2,
  input  CLKe,
  input  CLKs,
  input  gr,
  input  eq,
  input  zero,
  input  C,
  input  [7:0] in_9,
  output MARs,
  output BUS1,
  output IARe,
  output TEMPs,
  output RAMs,
  output ACCs,
  output IARs,
  output RAMe,
  output IRs,
  output FLAGs,
  output ACCe,
  output out_21,
  output REG_s0,
  output REGs_1,
  output REGs_2,
  output REG_e0,
  output REG_s3,
  output REG_e1,
  output REG_e2,
  output REG_e3,
  output END,
  output [2:0] out_31
);

  wire ACC_E_ALU, ACC_E_DT, ACC_E_JMPI, ACC_S_DT, ACC_S_JMPI, ALU_OP_SIGNAL, and_4_out, and_5_out, and_6_out,
       and_7_out, and_8_out, and_9_out, and_10_out, and_11_out, and_15_out, and_16_out, and_17_out,
       and_18_out, and_19_out, and_20_out, and_21_out, and_30_out, and_31_out, and_32_out, and_33_out,
       and_44_out, and_45_out, and_46_out, and_47_out, and_48_out, and_49_out, and_50_out, and_51_out,
       and_52_out, and_53_out, and_54_out, BUS_CLRF, counter_8_1_out_3, counter_8_1_out_4, counter_8_1_out_5,
       counter_8_1_out_6, counter_8_1_out_8, counter_8_1_out_9, cu_decoder_2x4_east_1_out_3,
       cu_decoder_2x4_east_1_out_4, cu_decoder_2x4_east_1_out_5, cu_decoder_2x4_east_1_out_6, decoder_1_out0,
       decoder_1_out1, decoder_1_out2, decoder_1_out3, decoder_1_out4, decoder_1_out5, decoder_1_out6,
       decoder_1_out7, IAR_E_JMPA, IAR_S_JMPA, IAR_S_JMPI1, IAR_S_JMPR, MAR_S_LD_STR, not_1_out, not_2_out,
       not_3_out, or_6_out, or_7_out, or_8_out, or_9_out, or_10_out, or_11_out, or_12_out, or_13_out,
       or_14_out, or_15_out, or_16_out, or_17_out, RAM_E_DT, RAM_E_LD, RAM_S_STR, REG_A_out_3, REG_A_out_4,
       REG_A_out_5, REG_A_out_6, REG_B_E_ALU, REG_B_out_3, REG_B_out_4, REG_B_out_5, REG_B_out_6;

  or or_1 (REG_e3, and_7_out, and_11_out);
  or or_2 (REG_e0, and_4_out, and_8_out);
  or or_3 (REG_e1, and_5_out, and_9_out);
  or or_4 (REG_e2, and_6_out, and_10_out);
  and and_1 (IARe, CLKe, or_6_out);
  and and_2 (RAMe, CLKe, or_7_out);
  and and_3 (ACCe, CLKe, or_8_out);
  and and_4 (and_4_out, CLKe, or_9_out, REG_B_out_3);
  and and_5 (and_5_out, CLKe, or_9_out, REG_B_out_4);
  and and_6 (and_6_out, CLKe, or_9_out, REG_B_out_5);
  and and_7 (and_7_out, CLKe, or_9_out, REG_B_out_6);
  or or_5 (BUS1, counter_8_1_out_3, ACC_S_JMPI, ACC_S_DT, BUS_CLRF);
  or or_6 (or_6_out, counter_8_1_out_3, IAR_E_JMPA, ACC_S_DT, ACC_S_JMPI);
  or or_7 (or_7_out, counter_8_1_out_4, IAR_S_JMPA, RAM_E_LD, RAM_E_DT, IAR_S_JMPI1);
  or or_8 (or_8_out, counter_8_1_out_5, ACC_E_DT, ACC_E_ALU, ACC_E_JMPI);
  and and_8 (and_8_out, CLKe, or_10_out, REG_A_out_3);
  and and_9 (and_9_out, CLKe, or_10_out, REG_A_out_4);
  and and_10 (and_10_out, CLKe, or_10_out, REG_A_out_5);
  and and_11 (and_11_out, CLKe, or_10_out, REG_A_out_6);
  and and_12 (out_31[2], ALU_OP_SIGNAL, in_9[6], in_9[7]);
  and and_13 (out_31[1], ALU_OP_SIGNAL, in_9[5], in_9[7]);
  and and_14 (out_31[0], ALU_OP_SIGNAL, in_9[4], in_9[7]);
  Decoder #(.select(3), .enable("false")) decoder_1 (
    .out0(decoder_1_out0), .out1(decoder_1_out1), .out2(decoder_1_out2), .out3(decoder_1_out3),
    .out4(decoder_1_out4), .out5(decoder_1_out5), .out6(decoder_1_out6), .out7(decoder_1_out7),
    .sel(in_9[6:4]));
  or or_9 (or_9_out, RAM_S_STR, IAR_S_JMPR, REG_B_E_ALU);
  or or_10 (or_10_out, MAR_S_LD_STR, out_21);
  not not_1 (not_1_out, in_9[7]);
  CU_DECODER_2X4 REG_B (
    .in_1(in_9[0]), .in_2(in_9[1]), .out_3(REG_B_out_3), .out_4(REG_B_out_4), .out_5(REG_B_out_5),
    .out_6(REG_B_out_6));
  CU_DECODER_2X4 REG_A (
    .in_1(in_9[2]), .in_2(in_9[3]), .out_3(REG_A_out_3), .out_4(REG_A_out_4), .out_5(REG_A_out_5),
    .out_6(REG_A_out_6));
  and and_15 (and_15_out, decoder_1_out0, not_1_out);
  and and_16 (and_16_out, decoder_1_out1, not_1_out);
  and and_17 (and_17_out, decoder_1_out2, not_1_out);
  and and_18 (and_18_out, decoder_1_out3, not_1_out);
  and and_19 (and_19_out, decoder_1_out4, not_1_out);
  and and_20 (and_20_out, decoder_1_out5, not_1_out);
  and and_21 (and_21_out, decoder_1_out6, not_1_out);
  // AND_Gate and_22 has open pins: in0=decoder_1_out7, in1=not_1_out, out=open
  COUNTER_8 counter_8_1 (
    .in_2(CLK), .out_3(counter_8_1_out_3), .out_4(counter_8_1_out_4), .out_5(counter_8_1_out_5),
    .out_6(counter_8_1_out_6), .out_7(ALU_OP_SIGNAL), .out_8(counter_8_1_out_8), .out_9(counter_8_1_out_9),
    .in_1(counter_8_1_out_9));
  or or_11 (or_11_out, and_15_out, and_16_out);
  and and_23 (BUS_CLRF, and_21_out, counter_8_1_out_6);
  and and_24 (MAR_S_LD_STR, or_11_out, counter_8_1_out_6);
  and and_25 (ACC_S_DT, and_17_out, counter_8_1_out_6);
  and and_26 (IAR_S_JMPR, and_18_out, counter_8_1_out_6);
  and and_27 (IAR_E_JMPA, and_19_out, counter_8_1_out_6);
  and and_28 (ACC_S_JMPI, and_20_out, counter_8_1_out_6);
  and and_29 (REG_B_E_ALU, counter_8_1_out_6, in_9[7]);
  and and_30 (and_30_out, gr, in_9[3]);
  and and_31 (and_31_out, eq, in_9[2]);
  and and_32 (and_32_out, zero, in_9[1]);
  and and_33 (and_33_out, C, in_9[0]);
  not not_2 (not_2_out, in_9[5]);
  and and_34 (IAR_S_JMPA, and_19_out, ALU_OP_SIGNAL);
  and and_35 (ACC_E_JMPI, and_20_out, ALU_OP_SIGNAL);
  not not_3 (not_3_out, in_9[4]);
  and and_36 (out_21, ALU_OP_SIGNAL, in_9[7]);
  and and_37 (RAM_E_LD, and_15_out, ALU_OP_SIGNAL);
  and and_38 (RAM_S_STR, and_16_out, ALU_OP_SIGNAL);
  and and_39 (RAM_E_DT, and_17_out, ALU_OP_SIGNAL);
  or or_12 (or_12_out, and_30_out, and_31_out, and_32_out, and_33_out);
  and and_40 (ACC_E_ALU, counter_8_1_out_8, in_9[7]);
  and and_41 (ACC_E_DT, and_17_out, counter_8_1_out_8);
  and and_42 (IAR_S_JMPI1, and_20_out, counter_8_1_out_8, or_12_out);
  and and_43 (END, in_9[7], in_9[6], not_2_out, not_3_out, in_9[3], in_9[2], in_9[1], in_9[0]);
  CU_DECODER_2X4_EAST cu_decoder_2x4_east_1 (
    .in_1(in_9[0]), .in_2(in_9[1]), .out_3(cu_decoder_2x4_east_1_out_3), .out_4(cu_decoder_2x4_east_1_out_4),
    .out_5(cu_decoder_2x4_east_1_out_5), .out_6(cu_decoder_2x4_east_1_out_6));
  or or_13 (or_13_out, RAM_E_DT, RAM_E_LD, ACC_E_ALU);
  and and_44 (and_44_out, CLKs, or_14_out);
  or or_14 (or_14_out, counter_8_1_out_3, MAR_S_LD_STR, ACC_S_DT, IAR_E_JMPA, ACC_S_JMPI);
  or or_15 (or_15_out, counter_8_1_out_3, out_21, ACC_S_DT, ACC_S_JMPI);
  or or_16 (or_16_out, counter_8_1_out_5, IAR_S_JMPA, IAR_S_JMPR, ACC_E_DT, IAR_S_JMPI1, ACC_E_JMPI);
  or or_17 (or_17_out, out_21, BUS_CLRF);
  and and_45 (and_45_out, CLKs, cu_decoder_2x4_east_1_out_3, or_13_out);
  and and_46 (and_46_out, CLKs, cu_decoder_2x4_east_1_out_4, or_13_out);
  and and_47 (and_47_out, CLKs, cu_decoder_2x4_east_1_out_5, or_13_out);
  and and_48 (and_48_out, CLKs, cu_decoder_2x4_east_1_out_6, or_13_out);
  and and_49 (and_49_out, CLKs, REG_B_E_ALU);
  and and_50 (and_50_out, CLKs, RAM_S_STR);
  and and_51 (and_51_out, CLKs, or_15_out);
  and and_52 (and_52_out, CLKs, or_16_out);
  and and_53 (and_53_out, CLKs, counter_8_1_out_4);
  and and_54 (and_54_out, CLKs, or_17_out);
  or or_18 (MARs, in_2, and_44_out);
  or or_19 (TEMPs, in_2, and_49_out);
  or or_20 (RAMs, in_2, and_50_out);
  or or_21 (ACCs, in_2, and_51_out);
  or or_22 (IARs, in_2, and_52_out);
  or or_23 (IRs, in_2, and_53_out);
  or or_24 (FLAGs, in_2, and_54_out);
  or or_25 (REG_s0, in_2, and_45_out);
  or or_26 (REGs_1, in_2, and_46_out);
  or or_27 (REGs_2, in_2, and_47_out);
  or or_28 (REG_s3, in_2, and_48_out);

  // Other names for the same wires on the sheet: FLAG_S_CLRF = BUS_CLRF; IAR_S_DT = ACC_E_DT; IAR_S_JMPI = ACC_E_JMPI;
  //   BUS_DT = ACC_S_DT; IAR_E_DT = ACC_S_DT; MAR_S_DT = ACC_S_DT; MAR_S_JMPA = IAR_E_JMPA; BUS_JMPI = ACC_S_JMPI;
  //   IAR_E_JMPI = ACC_S_JMPI; MAR_S_JMPI = ACC_S_JMPI; RAM_E_JMPA = IAR_S_JMPA; RAM_E_JMPI = IAR_S_JMPI1;
  //   REB_B_E_JMPR = IAR_S_JMPR; ACC_S_ALU = out_21; FLAG_S_ALU = out_21; REG_A_E_ALU = out_21;
  //   REG_A_E_LD_STR = MAR_S_LD_STR; REG_B_E_STR = RAM_S_STR; REG_B_S_ALU = ACC_E_ALU; REG_B_S_DT = RAM_E_DT;
  //   REG_B_S_LD = RAM_E_LD; TEMP_S_ALU = REG_B_E_ALU

  // Notes on the sheet:
  //   ALU_LINE
endmodule

module CU_DECODER_2X4 (
  input  in_1,
  input  in_2,
  output out_3,
  output out_4,
  output out_5,
  output out_6
);

  Decoder #(.select(2), .enable("false")) decoder_1 (
    .out0(out_3), .out1(out_4), .out2(out_5), .out3(out_6), .sel({in_2, in_1}));
endmodule

module CU_DECODER_2X4_EAST (
  input  in_1,
  input  in_2,
  output out_3,
  output out_4,
  output out_5,
  output out_6
);

  Decoder #(.select(2), .enable("false")) decoder_1 (
    .out0(out_3), .out1(out_4), .out2(out_5), .out3(out_6), .sel({in_2, in_1}));
endmodule

module CPU_FLAG_REG (
  input  in_1,
  input  in_2,
  input  in_3,
  input  in_4,
  input  in_5,
  output out_6,
  output out_7,
  output out_8,
  output out_9
);

  MEM_1_BIT mem_1_bit_1 (.D(in_1), .E(in_5), .out_3(out_6));
  MEM_1_BIT mem_1_bit_2 (.D(in_2), .E(in_5), .out_3(out_7));
  MEM_1_BIT mem_1_bit_3 (.D(in_3), .E(in_5), .out_3(out_8));
  MEM_1_BIT mem_1_bit_4 (.D(in_4), .E(in_5), .out_3(out_9));

  // Notes on the sheet:
  //   in_1: pull=down
  //   in_2: pull=down
  //   in_4: pull=down
  //   in_3: pull=down
endmodule

module CPU_CARRY_TEMP (
  input  in_1,
  input  in_2,
  output out_3
);

  MEM_1_BIT mem_1_bit_1 (.D(in_1), .E(in_2), .out_3(out_3));

  // Notes on the sheet:
  //   in_1: pull=down
endmodule
